// Digital circuit CPU.dig as structural Verilog
module CPU (
  input  clk,
  input  [7:0] Input,
  output [7:0] Output
);

  wire and_1_out, and_2_out, and_3_out, and_4_out, and_5_out, and_6_out, and_7_out, and_8_out, and_9_out,
       and_10_out, and_11_out, and_12_out, and_13_out, and_14_out, and_15_out, and_16_out, and_17_out,
       and_18_out, and_19_out, and_20_out, and_21_out, and_22_out, and_23_out, and_24_out, and_25_out,
       and_26_out, and_27_out, and_28_out, and_29_out, and_30_out, and_31_out, and_33_out, button_1_out,
       Clk_t, comparator_1_eq, comparator_2_eq, delay_1_out, delay_2_out, delay_3_out, delay_4_out,
       delay_5_out, dipswitch_1_out, not_2_out, not_3_out, not_4_out, not_5_out, not_6_out, not_7_out,
       not_8_out, or_1_out, or_2_out, or_3_out, or_4_out, or_5_out, or_6_out, or_7_out, or_8_out, or_9_out,
       or_10_out, or_11_out, Proceed, rs_ff_1_q, rs_ff_2_q, rs_ff_3_q, rs_ff_as_1_q, rs_ff_as_2_nq,
       rs_ff_as_2_q, rs_ff_as_3_nq, Send_out;
  wire [7:0] Changer_out, Data_d, driver_1_out, not_1_out, rom_1_d;
  wire [14:0] Depth_out, register_1_q, sub_1_s;
  wire [15:0] Pointer_out, ProgAddr;

  ROM #(.AddrBits(16), .Bits(8)) rom_1 (.A(ProgAddr), .sel(1'b1), .D(rom_1_d));
  assign not_1_out = ~rom_1_d;  // Not not_1, 8 bits wide
  and and_1 (and_1_out, rom_1_d[0], rom_1_d[1], not_1_out[2], rom_1_d[3]);
  and and_2 (and_2_out, rom_1_d[0], not_1_out[1], rom_1_d[2], rom_1_d[3]);
  and and_3 (and_3_out, not_1_out[4], rom_1_d[5], not_1_out[6], not_1_out[7]);
  and and_4 (and_4_out, not_1_out[0], not_1_out[1], rom_1_d[2], rom_1_d[3]);
  and and_5 (and_5_out, not_1_out[0], rom_1_d[1], rom_1_d[2], rom_1_d[3]);
  and and_6 (and_6_out, rom_1_d[4], rom_1_d[5], not_1_out[6], not_1_out[7]);
  and and_7 (and_7_out, rom_1_d[4], not_1_out[5], rom_1_d[6], not_1_out[7]);
  DipSwitch dipswitch_1 (.out(dipswitch_1_out));
  Button button_1 (.out(button_1_out));
  Multiplexer multiplexer_1 (.sel(dipswitch_1_out), .in_0(button_1_out), .in_1(clk), .out(Clk_t));
  and and_8 (and_8_out, and_1_out, and_3_out);
  and and_9 (and_9_out, and_2_out, and_3_out);
  and and_10 (and_10_out, and_4_out, and_3_out);
  and and_11 (and_11_out, and_5_out, and_3_out);
  and and_12 (and_12_out, and_4_out, and_6_out);
  and and_13 (and_13_out, and_5_out, and_6_out);
  and and_14 (and_14_out, and_1_out, and_7_out);
  and and_15 (and_15_out, and_2_out, and_7_out);
  not not_2 (not_2_out, or_1_out);
  or or_1 (or_1_out, or_1_out, and_16_out);
  and and_16 (and_16_out, Clk_t, Proceed);
  LED led_1 (.in(and_8_out));
  LED led_2 (.in(and_9_out));
  LED led_3 (.in(and_10_out));
  LED led_4 (.in(and_11_out));
  LED led_5 (.in(and_12_out));
  LED led_6 (.in(and_13_out));
  LED led_7 (.in(and_14_out));
  LED led_8 (.in(and_15_out));
  or or_2 (or_2_out, rs_ff_3_q, not_2_out);
  RS_FF rs_ff_1 (.S(or_2_out), .C(and_16_out), .R(rs_ff_1_q), .Q(rs_ff_1_q));  // open: nQ
  Delay #(.delayTime(4)) delay_1 (.in(and_14_out), .out(delay_1_out));
  Delay #(.delayTime(4)) delay_2 (.in(and_15_out), .out(delay_2_out));
  LED led_9 (.in(rs_ff_1_q));
  and and_17 (and_17_out, not_5_out, rs_ff_1_q);
  and and_18 (and_18_out, and_23_out, and_9_out);
  or or_3 (or_3_out, and_8_out, and_9_out);
  and and_19 (and_19_out, and_23_out, and_10_out);
  and and_20 (and_20_out, and_17_out, and_11_out);
  and and_21 (and_21_out, and_17_out, and_12_out);
  and and_22 (and_22_out, and_17_out, and_13_out);
  or or_4 (or_4_out, delay_2_out, and_15_out);
  or or_5 (or_5_out, delay_2_out, and_14_out);
  RS_FF rs_ff_2 (.S(rs_ff_1_q), .C(and_16_out), .R(rs_ff_2_q), .Q(rs_ff_2_q));  // open: nQ
  Comparator #(.Bits(8)) comparator_1 (.a(Data_d), .b({8{1'b0}}), .eq(comparator_1_eq));  // open: gt, lt
  Delay #(.delayTime(2)) delay_3 (.in(or_5_out), .out(delay_3_out));
  not not_3 (not_3_out, delay_3_out);
  LED led_10 (.in(rs_ff_2_q));
  and and_23 (and_23_out, not_5_out, rs_ff_2_q);
  and and_24 (and_24_out, and_17_out, or_3_out);
  and and_25 (and_25_out, and_23_out, or_3_out);
  not not_4 (not_4_out, comparator_1_eq);
  and and_26 (and_26_out, or_5_out, not_3_out);
  RS_FF rs_ff_3 (.S(rs_ff_2_q), .C(and_16_out), .R(rs_ff_3_q), .Q(rs_ff_3_q));  // open: nQ
  CounterPreset #(.Bits(15)) Depth (
    .en(1'b1), .C(and_26_out), .dir(or_4_out), .in({15{1'b0}}), .ld(1'b0), .clr(1'b0), .out(Depth_out));  // open: ovf
  LED led_11 (.in(rs_ff_3_q));
  and and_27 (and_27_out, not_5_out, rs_ff_3_q);
  or or_6 (or_6_out, and_25_out, and_19_out);
  or or_7 (or_7_out, and_24_out, and_20_out);
  RS_FF_AS rs_ff_as_1 (.S(and_29_out), .R(and_30_out), .Q(rs_ff_as_1_q));  // open: nQ
  and and_28 (and_28_out, comparator_1_eq, delay_1_out);
  and and_29 (and_29_out, not_4_out, delay_2_out);
  // Probe on Depth_out
  or or_8 (or_8_out, and_28_out, and_29_out);
  Sub #(.Bits(15)) sub_1 (.a(Depth_out), .b({15{1'b0}}), .c_i(and_28_out), .s(sub_1_s));  // open: c_o
  not not_5 (not_5_out, rs_ff_as_2_q);
  RS_FF_AS rs_ff_as_2 (.S(or_8_out), .R(and_30_out), .Q(rs_ff_as_2_q), .nQ(rs_ff_as_2_nq));
  or or_9 (or_9_out, and_27_out, rs_ff_as_2_q);
  or or_10 (or_10_out, and_22_out, and_21_out);
  and and_30 (and_30_out, comparator_2_eq, and_31_out);
  Comparator #(.Bits(15)) comparator_2 (.a(Depth_out), .b(register_1_q), .eq(comparator_2_eq));  // open: gt, lt
  Register #(.Bits(15)) register_1 (.D(sub_1_s), .C(or_8_out), .en(1'b1), .Q(register_1_q));
  CounterPreset #(.Bits(16)) Counter (
    .en(or_9_out), .C(Clk_t), .dir(rs_ff_as_1_q), .in({16{1'b0}}), .ld(1'b0), .clr(1'b0), .out(ProgAddr));  // open: ovf
  and and_31 (and_31_out, not_6_out, or_11_out);
  not not_6 (not_6_out, or_8_out);
  // Probe on register_1_q
  or or_11 (or_11_out, delay_4_out, and_7_out);
  Delay #(.delayTime(4)) delay_4 (.in(and_14_out), .out(delay_4_out));
  CounterPreset #(.Bits(16)) Pointer (
    .en(or_10_out), .C(Clk_t), .dir(and_21_out), .in({16{1'b0}}), .ld(1'b0), .clr(1'b0), .out(Pointer_out));  // open: ovf
  not not_7 (not_7_out, Clk_t);
  Delay delay_5 (.in(and_19_out), .out(delay_5_out));
  not not_8 (not_8_out, delay_5_out);
  and and_32 (Proceed, rs_ff_as_2_nq, rs_ff_as_3_nq);
  // Probe on ProgAddr
  // Probe on Pointer_out
  RAMDualPort #(.AddrBits(16), .Bits(8)) Data (
    .A(Pointer_out), .Din(driver_1_out), .str(or_6_out), .C(Clk_t), .ld(1'b1), .D(Data_d));
  and and_33 (and_33_out, and_19_out, not_8_out);
  // Probe on Data_d
  assign driver_1_out = or_7_out ? Data_d : 8'bz;  // Driver driver_1
  CounterPreset #(.Bits(8)) Changer (
    .en(1'b1), .C(not_7_out), .dir(and_18_out), .in(driver_1_out), .ld(and_24_out), .clr(1'b0),
    .out(Changer_out));  // open: ovf
  assign driver_1_out = and_25_out ? Changer_out : 8'bz;  // Driver driver_2
  assign driver_1_out = and_19_out ? Input : 8'bz;  // Driver driver_3
  RS_FF_AS rs_ff_as_3 (.S(and_33_out), .R(Send_out), .nQ(rs_ff_as_3_nq));  // open: Q
  Register #(.Bits(8)) register_2 (.D(driver_1_out), .C(Clk_t), .en(and_20_out), .Q(Output));
  Button Send (.out(Send_out));
  LED led_12 (.in(and_20_out));

  // Notes on the sheet:
  //   clk: Hz: 10
  //   + -
  //   , .
  //   < >
  //   [ ]
  //   rom_1 loads program.bf
  //   +
  //   -
  //   ,
  //   .
  //   <
  //   >
  //   [
  //   ]
  //   Counter_Inc
  //   Pointer_Inc
  //   Pointer_Dec
  //   Changer_Sub
  //   Changer_In
  //   Changer_Out
  //   Input_Out
  //   Input_Await
  //   Output_In
  //   Data_In
  //   Data_Out
endmodule
